# Fritzing sketch metal sensor and no touch button new version (saved by Fritzing 0.9.2b)
circuit board: 11.6887cm x 7.89263cm
breadboards: 1

parts:
  Led_1 = LED - 3mm [color="Red (660nm)" package="3 mm [THT]"]
  Led_2 = LED - 3mm [color="Green (560nm)" package="3 mm [THT]"]
  Av-Parking_System = Arduino Uno (Rev3) - ICSP
  Gnd_in1_in2_vcc = male pin header, 4 pins [form="♂ (male)"]
  Gnd_in1_in2_vcc1 = male pin header, 4 pins [form="♂ (male)"]
  R1 = Resistor [tolerance=±5% resistance=220 package=THT]
  J1 = male pin header, 2 pins [form="♂ (male)"]

nets:
  N1: Led_1.cathode, Av-Parking_System.D2
  N2: Led_1.anode, Led_2.anode, Av-Parking_System.GND, Gnd_in1_in2_vcc1.pin2, Gnd_in1_in2_vcc1.pin3, J1.pin2
  N3: Led_2.cathode, Av-Parking_System.D3_PWM
  N4: Av-Parking_System.A5/SCL, Gnd_in1_in2_vcc1.pin4
  N5: Av-Parking_System.D8, R1.Pin_1
  N6: Av-Parking_System.D7, Gnd_in1_in2_vcc1.pin1
  N7: Av-Parking_System.5V, Gnd_in1_in2_vcc.pin4
  N8: Av-Parking_System.VIN, J1.pin1
